// Logisim project bscs22017-bscs22101-bscs22131.circ as structural Verilog: 51 circuits, main circuit Add
module Add (
  input  A,
  input  B,
  input  Cin,
  output Sum,
  output Cout
);

  wire and_1_out, and_2_out, xor_1_out;

  and and_1 (and_1_out, B, A);
  xor xor_1 (xor_1_out, B, A);
  xor xor_2 (Sum, xor_1_out, Cin);
  and and_2 (and_2_out, xor_1_out, Cin);
  or or_1 (Cout, and_1_out, and_2_out);
endmodule

module FullAdd (
  input  Cin,
  input  [7:0] A,
  input  [7:0] B,
  output [7:0] AaddB,
  output Cout
);

  wire add_1_cout, add_2_cout, add_3_cout, add_4_cout, add_5_cout, add_6_cout, add_7_cout;

  Add add_1 (.A(A[0]), .B(B[0]), .Cin(Cin), .Sum(AaddB[0]), .Cout(add_1_cout));
  Add add_2 (.A(A[1]), .B(B[1]), .Cin(add_1_cout), .Sum(AaddB[1]), .Cout(add_2_cout));
  Add add_3 (.A(A[2]), .B(B[2]), .Cin(add_2_cout), .Sum(AaddB[2]), .Cout(add_3_cout));
  Add add_4 (.A(A[3]), .B(B[3]), .Cin(add_3_cout), .Sum(AaddB[3]), .Cout(add_4_cout));
  Add add_5 (.A(A[4]), .B(B[4]), .Cin(add_4_cout), .Sum(AaddB[4]), .Cout(add_5_cout));
  Add add_6 (.A(A[5]), .B(B[5]), .Cin(add_5_cout), .Sum(AaddB[5]), .Cout(add_6_cout));
  Add add_7 (.A(A[6]), .B(B[6]), .Cin(add_6_cout), .Sum(AaddB[6]), .Cout(add_7_cout));
  Add add_8 (.A(A[7]), .B(B[7]), .Cin(add_7_cout), .Sum(AaddB[7]), .Cout(Cout));
endmodule

module eightBitLS (
  input  [7:0] A,
  output [7:0] LS
);

  xor xor_1 (LS[0], A[0], A[0]);

  assign LS[7:1] = A[6:0];
endmodule

module Sub (
  input  A,
  input  B,
  input  Bin,
  output O,
  output Bout
);

  wire and_1_out, not_1_out, xor_1_out;

  not not_1 (not_1_out, A);
  xor xor_1 (xor_1_out, A, B);
  and and_1 (and_1_out, not_1_out, B);
  xor xor_2 (O, xor_1_out, Bin);
  or or_1 (Bout, and_1_out, Bin);
endmodule

module MainALU (
  input  Cin,
  input  [7:0] A,
  input  [7:0] B,
  input  S2,
  input  S1,
  input  S0,
  input  S3,
  output Cout,
  output Bout,
  output [7:0] O
);

  wire [7:0] eightbitand_1_aandb, eightbitls_1_ls, eightbitnot_1_anot, eightbitor_1_aorb, eightbitrs_1_rs,
       eightbitxor_1_axorb, fulladd_1_aaddb, fullsub_1_o, twoeightbitmux_1_o, twoeightbitmux_2_o,
       twoeightbitmux_3_o;

  FullAdd fulladd_1 (.Cin(Cin), .A(A), .B(B), .AaddB(fulladd_1_aaddb), .Cout(Cout));
  eightBitOr eightbitor_1 (.A(A), .B(B), .AorB(eightbitor_1_aorb));
  FullSub fullsub_1 (.A(A), .B(B), .O(fullsub_1_o), .Bout(Bout));
  eightBitAnd eightbitand_1 (.A(A), .B(B), .AandB(eightbitand_1_aandb));
  twoEightBitMux twoeightbitmux_1 (.S(S3), .A(A), .B(B), .O(twoeightbitmux_1_o));
  twoEightBitMux twoeightbitmux_2 (.S(S3), .A(A), .B(B), .O(twoeightbitmux_2_o));
  eightBitXor eightbitxor_1 (.A(A), .B(B), .AxorB(eightbitxor_1_axorb));
  twoEightBitMux twoeightbitmux_3 (.S(S3), .A(A), .B(B), .O(twoeightbitmux_3_o));
  eightBitNot eightbitnot_1 (.A(twoeightbitmux_1_o), .Anot(eightbitnot_1_anot));
  eightBitRS eightbitrs_1 (.A(twoeightbitmux_2_o), .RS(eightbitrs_1_rs));
  eightBitLS eightbitls_1 (.A(twoeightbitmux_3_o), .LS(eightbitls_1_ls));
  EightBitOutputsMux eightbitoutputsmux_1 (
    .S2(S2), .S1(S1), .S0(S0), .A0(fulladd_1_aaddb), .A1(eightbitor_1_aorb), .A2(fullsub_1_o),
    .A3(eightbitand_1_aandb), .A4(eightbitnot_1_anot), .A5(eightbitrs_1_rs), .A6(eightbitxor_1_axorb),
    .A7(eightbitls_1_ls), .O(O));

  // Notes on the sheet:
  //   0 -> A
  //   1 -> B
  //   000   ADD
  //   001   OR   
  //   010   SUB
  //   011   AND
  //   100   NOT
  //   101   RS   
  //   110   XOR
  //   111   LS  
endmodule

module eightBitOr (
  input  [7:0] A,
  input  [7:0] B,
  output [7:0] AorB
);

  or or_1 (AorB[0], B[0], A[0]);
  or or_2 (AorB[1], B[1], A[1]);
  or or_3 (AorB[2], B[2], A[2]);
  or or_4 (AorB[3], B[3], A[3]);
  or or_5 (AorB[4], B[4], A[4]);
  or or_6 (AorB[5], B[5], A[5]);
  or or_7 (AorB[6], B[6], A[6]);
  or or_8 (AorB[7], B[7], A[7]);
endmodule

module eightBitAnd (
  input  [7:0] A,
  input  [7:0] B,
  output [7:0] AandB
);

  and and_1 (AandB[0], B[0], A[0]);
  and and_2 (AandB[1], B[1], A[1]);
  and and_3 (AandB[2], B[2], A[2]);
  and and_4 (AandB[3], B[3], A[3]);
  and and_5 (AandB[4], B[4], A[4]);
  and and_6 (AandB[5], B[5], A[5]);
  and and_7 (AandB[6], B[6], A[6]);
  and and_8 (AandB[7], B[7], A[7]);
endmodule

module eightBitNot (
  input  [7:0] A,
  output [7:0] Anot
);

  not not_1 (Anot[0], A[0]);
  not not_2 (Anot[1], A[1]);
  not not_3 (Anot[2], A[2]);
  not not_4 (Anot[3], A[3]);
  not not_5 (Anot[4], A[4]);
  not not_6 (Anot[5], A[5]);
  not not_7 (Anot[6], A[6]);
  not not_8 (Anot[7], A[7]);
endmodule

module eightBitXor (
  input  [7:0] A,
  input  [7:0] B,
  output [7:0] AxorB
);

  xor xor_1 (AxorB[0], B[0], A[0]);
  xor xor_2 (AxorB[1], B[1], A[1]);
  xor xor_3 (AxorB[2], B[2], A[2]);
  xor xor_4 (AxorB[3], B[3], A[3]);
  xor xor_5 (AxorB[4], B[4], A[4]);
  xor xor_6 (AxorB[5], B[5], A[5]);
  xor xor_7 (AxorB[6], B[6], A[6]);
  xor xor_8 (AxorB[7], B[7], A[7]);
endmodule

module eightBitRS (
  input  [7:0] A,
  output [7:0] RS
);

  xor xor_1 (RS[7], A[7], A[7]);

  assign RS[6:0] = A[7:1];
endmodule

module eightBitMux (
  input  S2,
  input  S1,
  input  S0,
  input  A0,
  input  A1,
  input  A2,
  input  A3,
  input  A4,
  input  A5,
  input  A6,
  input  A7,
  output O
);

  wire and_1_out, and_2_out, and_3_out, and_4_out, and_5_out, and_6_out, and_7_out, and_8_out, not_1_out,
       not_2_out, not_3_out;

  not not_1 (not_1_out, S2);
  not not_2 (not_2_out, S1);
  not not_3 (not_3_out, S0);
  and and_1 (and_1_out, A0, not_1_out, not_2_out, not_3_out);
  and and_2 (and_2_out, A1, not_1_out, not_2_out, S0);
  and and_3 (and_3_out, A2, not_1_out, S1, not_3_out);
  and and_4 (and_4_out, A3, S0, S1, not_1_out);
  and and_5 (and_5_out, A4, S2, not_2_out, not_3_out);
  and and_6 (and_6_out, A5, S2, not_2_out, S0);
  and and_7 (and_7_out, A6, S2, S1, not_3_out);
  and and_8 (and_8_out, A7, S2, S1, S0);
  or or_1 (O, and_1_out, and_2_out, and_3_out, and_4_out, and_5_out, and_6_out, and_7_out, and_8_out);
endmodule

module FullSub (
  input  [7:0] A,
  input  [7:0] B,
  output [7:0] O,
  output Bout
);

  wire add_1_cout, add_2_cout, add_3_cout, add_4_cout, add_5_cout, add_6_cout, add_7_cout, xor_1_out,
       xor_2_out, xor_3_out, xor_4_out, xor_5_out, xor_6_out, xor_7_out, xor_8_out;

  xor xor_1 (xor_1_out, 1'b1, B[0]);
  xor xor_2 (xor_2_out, B[1], 1'b1);
  xor xor_3 (xor_3_out, B[2], 1'b1);
  xor xor_4 (xor_4_out, B[3], 1'b1);
  xor xor_5 (xor_5_out, B[4], 1'b1);
  xor xor_6 (xor_6_out, B[5], 1'b1);
  xor xor_7 (xor_7_out, B[6], 1'b1);
  xor xor_8 (xor_8_out, B[7], 1'b1);
  Add add_1 (.A(A[0]), .B(xor_1_out), .Cin(1'b1), .Sum(O[0]), .Cout(add_1_cout));
  Add add_2 (.A(A[1]), .B(xor_2_out), .Cin(add_1_cout), .Sum(O[1]), .Cout(add_2_cout));
  Add add_3 (.A(A[2]), .B(xor_3_out), .Cin(add_2_cout), .Sum(O[2]), .Cout(add_3_cout));
  Add add_4 (.A(A[3]), .B(xor_4_out), .Cin(add_3_cout), .Sum(O[3]), .Cout(add_4_cout));
  Add add_5 (.A(A[4]), .B(xor_5_out), .Cin(add_4_cout), .Sum(O[4]), .Cout(add_5_cout));
  Add add_6 (.A(A[5]), .B(xor_6_out), .Cin(add_5_cout), .Sum(O[5]), .Cout(add_6_cout));
  Add add_7 (.A(A[6]), .B(xor_7_out), .Cin(add_6_cout), .Sum(O[6]), .Cout(add_7_cout));
  Add add_8 (.A(A[7]), .B(xor_8_out), .Cin(add_7_cout), .Sum(O[7]), .Cout(Bout));
endmodule

module oneBitMux (
  input  S,
  input  A,
  input  B,
  output O
);

  wire and_1_out, and_2_out, not_1_out;

  not not_1 (not_1_out, S);
  and and_1 (and_1_out, S, B);
  and and_2 (and_2_out, not_1_out, A);
  or or_1 (O, and_2_out, and_1_out);
endmodule

module twoEightBitMux (
  input  S,
  input  [7:0] A,
  input  [7:0] B,
  output [7:0] O
);

  oneBitMux onebitmux_1 (.S(S), .A(A[0]), .B(B[0]), .O(O[0]));
  oneBitMux onebitmux_2 (.S(S), .A(A[1]), .B(B[1]), .O(O[1]));
  oneBitMux onebitmux_3 (.S(S), .A(A[2]), .B(B[2]), .O(O[2]));
  oneBitMux onebitmux_4 (.S(S), .A(A[3]), .B(B[3]), .O(O[3]));
  oneBitMux onebitmux_5 (.S(S), .A(A[4]), .B(B[4]), .O(O[4]));
  oneBitMux onebitmux_6 (.S(S), .A(A[5]), .B(B[5]), .O(O[5]));
  oneBitMux onebitmux_7 (.S(S), .A(A[6]), .B(B[6]), .O(O[6]));
  oneBitMux onebitmux_8 (.S(S), .A(A[7]), .B(B[7]), .O(O[7]));
endmodule

module EightBitOutputsMux (
  input  S2,
  input  S1,
  input  S0,
  input  [7:0] A0,
  input  [7:0] A1,
  input  [7:0] A2,
  input  [7:0] A3,
  input  [7:0] A4,
  input  [7:0] A5,
  input  [7:0] A6,
  input  [7:0] A7,
  output [7:0] O
);

  eightBitMux eightbitmux_1 (
    .S2(S2), .S1(S1), .S0(S0), .A0(A0[0]), .A1(A1[0]), .A2(A2[0]), .A3(A3[0]), .A4(A4[0]), .A5(A5[0]),
    .A6(A6[0]), .A7(A7[0]), .O(O[0]));
  eightBitMux eightbitmux_2 (
    .S2(S2), .S1(S1), .S0(S0), .A0(A0[1]), .A1(A1[1]), .A2(A2[1]), .A3(A3[1]), .A4(A4[1]), .A5(A5[1]),
    .A6(A6[1]), .A7(A7[1]), .O(O[1]));
  eightBitMux eightbitmux_3 (
    .S2(S2), .S1(S1), .S0(S0), .A0(A0[2]), .A1(A1[2]), .A2(A2[2]), .A3(A3[2]), .A4(A4[2]), .A5(A5[2]),
    .A6(A6[2]), .A7(A7[2]), .O(O[2]));
  eightBitMux eightbitmux_4 (
    .S2(S2), .S1(S1), .S0(S0), .A0(A0[3]), .A1(A1[3]), .A2(A2[3]), .A3(A3[3]), .A4(A4[3]), .A5(A5[3]),
    .A6(A6[3]), .A7(A7[3]), .O(O[3]));
  eightBitMux eightbitmux_5 (
    .S2(S2), .S1(S1), .S0(S0), .A0(A0[4]), .A1(A1[4]), .A2(A2[4]), .A3(A3[4]), .A4(A4[4]), .A5(A5[4]),
    .A6(A6[4]), .A7(A7[4]), .O(O[4]));
  eightBitMux eightbitmux_6 (
    .S2(S2), .S1(S1), .S0(S0), .A0(A0[5]), .A1(A1[5]), .A2(A2[5]), .A3(A3[5]), .A4(A4[5]), .A5(A5[5]),
    .A6(A6[5]), .A7(A7[5]), .O(O[5]));
  eightBitMux eightbitmux_7 (
    .S2(S2), .S1(S1), .S0(S0), .A0(A0[6]), .A1(A1[6]), .A2(A2[6]), .A3(A3[6]), .A4(A4[6]), .A5(A5[6]),
    .A6(A6[6]), .A7(A7[6]), .O(O[6]));
  eightBitMux eightbitmux_8 (
    .S2(S2), .S1(S1), .S0(S0), .A0(A0[7]), .A1(A1[7]), .A2(A2[7]), .A3(A3[7]), .A4(A4[7]), .A5(A5[7]),
    .A6(A6[7]), .A7(A7[7]), .O(O[7]));
endmodule

module parityCheck (
  input  [7:0] PayLoad,
  input  PB,
  output O
);

  wire xor_1_out, xor_2_out, xor_3_out, xor_4_out, xor_5_out, xor_6_out, xor_7_out;

  xor xor_1 (xor_1_out, PayLoad[0], PayLoad[1]);
  xor xor_2 (xor_2_out, PayLoad[2], PayLoad[3]);
  xor xor_3 (xor_3_out, PayLoad[4], PayLoad[5]);
  xor xor_4 (xor_4_out, PayLoad[6], PayLoad[7]);
  xor xor_5 (xor_5_out, xor_1_out, xor_2_out);
  xor xor_6 (xor_6_out, xor_3_out, xor_4_out);
  xor xor_7 (xor_7_out, xor_5_out, xor_6_out);
  xor xor_8 (O, xor_7_out, PB);
endmodule

module BCDdecode (
  input  A,
  input  C,
  input  B,
  output [7:0] O
);

  wire not_1_out, not_2_out, not_3_out;

  not not_1 (not_1_out, A);
  not not_2 (not_2_out, B);
  not not_3 (not_3_out, C);
  and and_1 (O[0], not_1_out, not_2_out, not_3_out);
  and and_2 (O[2], not_1_out, B, not_3_out);
  and and_3 (O[3], not_1_out, B, C);
  and and_4 (O[6], A, B, not_3_out);
  and and_5 (O[7], A, B, C);
  and and_6 (O[4], A, not_2_out, not_3_out);
  and and_7 (O[5], A, not_2_out, C);
  and and_8 (O[1], not_1_out, not_2_out, C);

  // Notes on the sheet:
  //   4
  //   2
  //   1
endmodule

module fourBitMux (
  input  S1,
  input  S0,
  input  A0,
  input  A1,
  input  A2,
  input  A3,
  output O
);

  wire and_1_out, and_2_out, and_3_out, and_4_out, not_1_out, not_2_out;

  not not_1 (not_1_out, S1);
  not not_2 (not_2_out, S0);
  and and_1 (and_1_out, A0, not_2_out, not_1_out);
  and and_2 (and_2_out, A1, S0, not_1_out);
  and and_3 (and_3_out, A2, not_2_out, S1);
  and and_4 (and_4_out, A3, S0, S1);
  or or_1 (O, and_1_out, and_2_out, and_3_out, and_4_out);
endmodule

module fourBitLeft (
  input  [3:0] A,
  output [3:0] LS
);

  xor xor_1 (LS[0], A[0], A[0]);

  assign LS[3:1] = A[2:0];
endmodule

module LsCheck (
  input  [1:0] S,
  input  [3:0] A,
  input  [3:0] B,
  output AequalsB
);

  LsBitsDecide lsbitsdecide_1 (.Control(S), .A(A), .B(B), .O(AequalsB));
endmodule

module LsBitsDecide (
  input  [1:0] Control,
  input  [3:0] A,
  input  [3:0] B,
  output O
);

  wire xor_1_out, xor_2_out, xor_3_out, xor_4_out;
  wire [3:0] fourbitleft_1_ls, fourbitleft_2_ls, fourbitleft_3_ls, fourbitleft_4_ls, fourbitleft_5_ls,
       fourbitleft_6_ls, fourbitmux_1_o;

  fourBitLeft fourbitleft_1 (.A(A), .LS(fourbitleft_1_ls));
  fourBitLeft fourbitleft_2 (.A(A), .LS(fourbitleft_2_ls));
  fourBitLeft fourbitleft_3 (.A(fourbitleft_2_ls), .LS(fourbitleft_3_ls));
  fourBitLeft fourbitleft_4 (.A(A), .LS(fourbitleft_4_ls));
  fourBitLeft fourbitleft_5 (.A(fourbitleft_4_ls), .LS(fourbitleft_5_ls));
  fourBitLeft fourbitleft_6 (.A(fourbitleft_5_ls), .LS(fourbitleft_6_ls));
  fourBitMux fourbitmux_1 (
    .S1(Control[1]), .S0(Control[0]), .A0(A[0]), .A1(A[1]), .A2(A[2]), .A3(A[3]), .O(fourbitmux_1_o[0]));
  fourBitMux fourbitmux_2 (
    .S1(Control[1]), .S0(Control[0]), .A0(fourbitleft_1_ls[0]), .A1(fourbitleft_1_ls[1]),
    .A2(fourbitleft_1_ls[2]), .A3(fourbitleft_1_ls[3]), .O(fourbitmux_1_o[1]));
  fourBitMux fourbitmux_3 (
    .S1(Control[1]), .S0(Control[0]), .A0(fourbitleft_3_ls[0]), .A1(fourbitleft_3_ls[1]),
    .A2(fourbitleft_3_ls[2]), .A3(fourbitleft_3_ls[3]), .O(fourbitmux_1_o[2]));
  fourBitMux fourbitmux_4 (
    .S1(Control[1]), .S0(Control[0]), .A0(fourbitleft_6_ls[0]), .A1(fourbitleft_6_ls[1]),
    .A2(fourbitleft_6_ls[2]), .A3(fourbitleft_6_ls[3]), .O(fourbitmux_1_o[3]));
  xor xor_1 (xor_1_out, B[0], fourbitmux_1_o[0]);
  xor xor_2 (xor_2_out, B[1], fourbitmux_1_o[1]);
  xor xor_3 (xor_3_out, B[2], fourbitmux_1_o[2]);
  xor xor_4 (xor_4_out, B[3], fourbitmux_1_o[3]);
  nor nor_1 (O, xor_1_out, xor_2_out, xor_3_out, xor_4_out);
endmodule

module main (
  input  in_1,
  input  in_2,
  input  in_3,
  input  in_4,
  input  in_5,
  input  in_6,
  input  in_7,
  input  in_8,
  input  in_9,
  input  in_10,
  input  in_11,
  input  in_12,
  input  in_13,
  input  in_14,
  input  in_15,
  output out_16
);

  wire onebitmux_1_o, onebitmux_2_o, onebitmux_3_o, onebitmux_4_o, onebitmux_5_o, onebitmux_6_o;

  oneBitMux onebitmux_1 (.S(in_5), .A(in_6), .B(in_7), .O(onebitmux_1_o));
  oneBitMux onebitmux_2 (.S(in_9), .A(in_10), .B(in_11), .O(onebitmux_2_o));
  oneBitMux onebitmux_3 (.S(in_13), .A(in_14), .B(in_15), .O(onebitmux_3_o));
  oneBitMux onebitmux_4 (.S(in_1), .A(in_2), .B(in_3), .O(onebitmux_4_o));
  oneBitMux onebitmux_5 (.S(in_4), .A(onebitmux_4_o), .B(onebitmux_1_o), .O(onebitmux_5_o));
  oneBitMux onebitmux_6 (.S(in_12), .A(onebitmux_2_o), .B(onebitmux_3_o), .O(onebitmux_6_o));
  oneBitMux onebitmux_7 (.S(in_8), .A(onebitmux_5_o), .B(onebitmux_6_o), .O(out_16));
endmodule

module towToFourDecod (
  input  A1,
  input  A0,
  output [3:0] out_3
);

  wire not_1_out, not_2_out;

  not not_1 (not_1_out, A1);
  not not_2 (not_2_out, A0);
  and and_1 (out_3[0], not_2_out, not_1_out);
  and and_2 (out_3[1], not_1_out, A0);
  and and_3 (out_3[2], A1, not_2_out);
  and and_4 (out_3[3], A1, A0);
endmodule

module DecodMain (
  input  in_1,
  input  in_2,
  input  in_3,
  input  in_4,
  input  in_5,
  input  in_6,
  output out_7
);

  wire and_1_out, and_2_out, and_3_out, and_4_out;
  wire [3:0] towtofourdecod_1_out_3;

  towToFourDecod towtofourdecod_1 (.A1(in_5), .A0(in_6), .out_3(towtofourdecod_1_out_3));
  and and_1 (and_1_out, in_1, towtofourdecod_1_out_3[0]);
  and and_2 (and_2_out, in_2, towtofourdecod_1_out_3[1]);
  and and_3 (and_3_out, in_3, towtofourdecod_1_out_3[2]);
  and and_4 (and_4_out, in_4, towtofourdecod_1_out_3[3]);
  or or_1 (out_7, and_1_out, and_2_out, and_3_out, and_4_out);
endmodule

module leftShiftMux (
  input  in_1,
  input  in_2,
  input  in_3,
  input  [7:0] A,
  output [7:0] out_5
);

  wire [7:0] eightbitls_1_ls, eightbitls_2_ls, eightbitls_3_ls, eightbitls_4_ls, eightbitls_5_ls,
       eightbitls_6_ls, eightbitls_7_ls;

  eightBitLS eightbitls_1 (.A(A), .LS(eightbitls_1_ls));
  eightBitLS eightbitls_2 (.A(eightbitls_1_ls), .LS(eightbitls_2_ls));
  eightBitLS eightbitls_3 (.A(eightbitls_2_ls), .LS(eightbitls_3_ls));
  eightBitLS eightbitls_4 (.A(eightbitls_3_ls), .LS(eightbitls_4_ls));
  eightBitLS eightbitls_5 (.A(eightbitls_4_ls), .LS(eightbitls_5_ls));
  eightBitLS eightbitls_6 (.A(eightbitls_5_ls), .LS(eightbitls_6_ls));
  eightBitLS eightbitls_7 (.A(eightbitls_6_ls), .LS(eightbitls_7_ls));
  EightBitOutputsMux eightbitoutputsmux_1 (
    .S2(in_1), .S1(in_2), .S0(in_3), .A0(A), .A1(eightbitls_1_ls), .A2(eightbitls_2_ls),
    .A3(eightbitls_3_ls), .A4(eightbitls_4_ls), .A5(eightbitls_5_ls), .A6(eightbitls_6_ls),
    .A7(eightbitls_7_ls), .O(out_5));
endmodule

module leftORright (
  input  in_1,
  input  in_2,
  input  in_3,
  input  in_4,
  input  in_5,
  input  [7:0] in_6,
  output [7:0] out_7,
  output [3:0] out_8,
  output out_9
);

  wire [3:0] countones_1_out_2, countones_2_out_2;
  wire [7:0] leftshiftmux_1_out_5, rightshiftmux_1_out_5;

  leftShiftMux leftshiftmux_1 (.in_1(in_1), .in_2(in_2), .in_3(in_3), .A(in_6), .out_5(leftshiftmux_1_out_5));
  rightShiftMux rightshiftmux_1 (.in_1(in_1), .in_2(in_2), .in_3(in_3), .A(in_6), .out_5(rightshiftmux_1_out_5));
  countOnes countones_1 (.in_1(in_6), .out_2(countones_1_out_2));  // open: out_3
  countOnes countones_2 (.in_1(out_7), .out_2(countones_2_out_2));  // open: out_3
  twoEightBitMux twoeightbitmux_1 (.S(in_4), .A(leftshiftmux_1_out_5), .B(rightshiftmux_1_out_5), .O(out_7));
  fourBitSub fourbitsub_1 (.Bin(in_5), .A(countones_1_out_2), .B(countones_2_out_2), .O(out_8), .Bout(out_9));
endmodule

module rightShiftMux (
  input  in_1,
  input  in_2,
  input  in_3,
  input  [7:0] A,
  output [7:0] out_5
);

  wire [7:0] eightbitrs_1_rs, eightbitrs_2_rs, eightbitrs_3_rs, eightbitrs_4_rs, eightbitrs_5_rs,
       eightbitrs_6_rs, eightbitrs_7_rs;

  eightBitRS eightbitrs_1 (.A(A), .RS(eightbitrs_1_rs));
  eightBitRS eightbitrs_2 (.A(eightbitrs_1_rs), .RS(eightbitrs_2_rs));
  eightBitRS eightbitrs_3 (.A(eightbitrs_2_rs), .RS(eightbitrs_3_rs));
  eightBitRS eightbitrs_4 (.A(eightbitrs_3_rs), .RS(eightbitrs_4_rs));
  eightBitRS eightbitrs_5 (.A(eightbitrs_4_rs), .RS(eightbitrs_5_rs));
  eightBitRS eightbitrs_6 (.A(eightbitrs_5_rs), .RS(eightbitrs_6_rs));
  eightBitRS eightbitrs_7 (.A(eightbitrs_6_rs), .RS(eightbitrs_7_rs));
  EightBitOutputsMux eightbitoutputsmux_1 (
    .S2(in_1), .S1(in_2), .S0(in_3), .A0(A), .A1(eightbitrs_1_rs), .A2(eightbitrs_2_rs),
    .A3(eightbitrs_3_rs), .A4(eightbitrs_4_rs), .A5(eightbitrs_5_rs), .A6(eightbitrs_6_rs),
    .A7(eightbitrs_7_rs), .O(out_5));
endmodule

module halfAdd (
  input  A,
  input  B,
  output Sum,
  output Cout
);

  and and_1 (Cout, B, A);
  xor xor_1 (Sum, B, A);
endmodule

module fourBitSub (
  input  Bin,
  input  [3:0] A,
  input  [3:0] B,
  output [3:0] O,
  output Bout
);

  wire sub_1_bout, sub_2_bout, sub_3_bout;

  Sub sub_1 (.A(A[0]), .B(B[0]), .Bin(Bin), .O(O[0]), .Bout(sub_1_bout));
  Sub sub_2 (.A(A[1]), .B(B[1]), .Bin(sub_1_bout), .O(O[1]), .Bout(sub_2_bout));
  Sub sub_3 (.A(A[2]), .B(B[2]), .Bin(sub_2_bout), .O(O[2]), .Bout(sub_3_bout));
  Sub sub_4 (.A(A[3]), .B(B[3]), .Bin(sub_3_bout), .O(O[3]), .Bout(Bout));
endmodule

module countOnes (
  input  [7:0] in_1,
  output [3:0] out_2,
  output [3:0] out_3
);

  wire add_1_cout, add_1_sum, add_2_cout, add_2_sum, add_3_cout, add_3_sum, add_4_cout, add_4_sum,
       add_5_cout, add_6_cout, add_7_cout, add_8_cout, halfadd_1_cout, halfadd_1_sum;

  Add add_1 (.A(in_1[0]), .B(in_1[1]), .Cin(in_1[2]), .Sum(add_1_sum), .Cout(add_1_cout));
  Add add_2 (.A(in_1[3]), .B(in_1[4]), .Cin(in_1[5]), .Sum(add_2_sum), .Cout(add_2_cout));
  halfAdd halfadd_1 (.A(in_1[6]), .B(in_1[7]), .Sum(halfadd_1_sum), .Cout(halfadd_1_cout));
  Add add_3 (.A(in_1[0]), .B(in_1[1]), .Cin(in_1[2]), .Sum(add_3_sum), .Cout(add_3_cout));
  Add add_4 (.A(in_1[3]), .B(in_1[4]), .Cin(in_1[5]), .Sum(add_4_sum), .Cout(add_4_cout));
  Add add_5 (.A(add_1_sum), .B(add_2_sum), .Cin(in_1[6]), .Sum(out_2[0]), .Cout(add_5_cout));
  Add add_6 (.A(add_1_cout), .B(add_2_cout), .Cin(add_5_cout), .Sum(out_2[1]), .Cout(add_6_cout));
  halfAdd halfadd_2 (.A(in_1[7]), .B(add_6_cout), .Sum(out_2[2]), .Cout(out_2[3]));
  Add add_7 (.A(add_3_sum), .B(add_4_sum), .Cin(halfadd_1_sum), .Sum(out_3[0]), .Cout(add_7_cout));
  Add add_8 (.A(add_3_cout), .B(add_4_cout), .Cin(add_7_cout), .Sum(out_3[1]), .Cout(add_8_cout));
  halfAdd halfadd_3 (.A(add_8_cout), .B(halfadd_1_cout), .Sum(out_3[2]), .Cout(out_3[3]));
endmodule

module threeToEightDecod (
  input  A,
  input  B,
  input  C,
  output [7:0] O
);

  wire not_1_out, not_2_out, not_3_out;

  not not_1 (not_1_out, A);
  not not_2 (not_2_out, B);
  not not_3 (not_3_out, C);
  and and_1 (O[0], not_1_out, not_2_out, not_3_out);
  and and_2 (O[1], not_1_out, not_2_out, C);
  and and_3 (O[2], not_1_out, B, not_3_out);
  and and_4 (O[3], not_1_out, B, C);
  and and_5 (O[4], A, not_2_out, not_3_out);
  and and_6 (O[5], A, not_2_out, C);
  and and_7 (O[6], A, B, not_3_out);
  and and_8 (O[7], A, B, C);
endmodule

module twoToFourDecodWithEnable (
  input  in_1,
  input  in_2,
  input  in_3,
  output [3:0] out_4
);

  wire and_1_out, and_2_out, and_3_out, and_4_out, not_1_out, not_2_out, not_3_out;

  not not_1 (not_1_out, in_1);
  not not_2 (not_2_out, in_2);
  and and_1 (and_1_out, not_2_out, not_1_out);
  and and_2 (and_2_out, not_1_out, in_2);
  and and_3 (and_3_out, in_1, not_2_out);
  and and_4 (and_4_out, in_1, in_2);
  not not_3 (not_3_out, in_3);
  and and_5 (out_4[0], and_1_out, not_3_out);
  and and_6 (out_4[1], and_2_out, not_3_out);
  and and_7 (out_4[2], and_3_out, not_3_out);
  and and_8 (out_4[3], and_4_out, not_3_out);
endmodule

module multiplyThreeBitByTwo (
  input  [2:0] in_1,
  output [3:0] out_2
);

  wire [7:0] threetoeightdecod_1_o;

  threeToEightDecod threetoeightdecod_1 (.A(in_1[0]), .B(in_1[1]), .C(in_1[2]), .O(threetoeightdecod_1_o));
  and and_1 (out_2[0], threetoeightdecod_1_o[0], threetoeightdecod_1_o[1]);
  or or_1 (out_2[1], threetoeightdecod_1_o[1], threetoeightdecod_1_o[3], threetoeightdecod_1_o[5], threetoeightdecod_1_o[7]);
  or or_2 (out_2[2], threetoeightdecod_1_o[2], threetoeightdecod_1_o[3], threetoeightdecod_1_o[6], threetoeightdecod_1_o[7]);
  or or_3 (out_2[3], threetoeightdecod_1_o[4], threetoeightdecod_1_o[5], threetoeightdecod_1_o[6], threetoeightdecod_1_o[7]);
endmodule

module D_flipflop (
  input  in_1,
  input  E,
  input  S,
  output Q
);

  wire nand_1_out, nand_2_out, nand_4_out, not_1_out, or_1_out;

  not not_1 (not_1_out, in_1);
  nand nand_1 (nand_1_out, in_1, E);
  nand nand_2 (nand_2_out, E, not_1_out);
  or or_1 (or_1_out, nand_2_out, S);
  nand nand_3 (Q, nand_1_out, nand_4_out);
  nand nand_4 (nand_4_out, Q, or_1_out);
endmodule

module SR_latch (
  input  R,
  input  S,
  output Q
);

  wire nor_2_out;

  nor nor_1 (Q, R, nor_2_out);
  nor nor_2 (nor_2_out, Q, S);
endmodule

module DFlipFlopWithComp (
  input  CLK,
  input  RST,
  output [2:0] A
);

  wire d_ff_1_qn, d_ff_2_qn, d_ff_3_qn;

  D_Flip_Flop d_ff_1 (.D(d_ff_1_qn), .clk(CLK), .Q(A[0]), .Qn(d_ff_1_qn), .reset(RST));  // open: preset
  D_Flip_Flop d_ff_2 (.D(d_ff_2_qn), .clk(d_ff_1_qn), .Q(A[1]), .Qn(d_ff_2_qn), .reset(RST));  // open: preset
  D_Flip_Flop d_ff_3 (.D(d_ff_3_qn), .clk(d_ff_2_qn), .Q(A[2]), .Qn(d_ff_3_qn), .reset(RST));  // open: preset
endmodule

module ThreeBitEqual (
  input  [2:0] A,
  input  [2:0] B,
  output O
);

  wire xnor_1_out, xnor_2_out, xnor_3_out;

  xnor xnor_1 (xnor_1_out, A[0], B[0]);
  xnor xnor_2 (xnor_2_out, B[1], A[1]);
  xnor xnor_3 (xnor_3_out, A[2], B[2]);
  and and_1 (O, xnor_1_out, xnor_2_out, xnor_3_out);
endmodule

module MultiFourBitMux (
  input  S2,
  input  S1,
  input  S0,
  input  [3:0] O0,
  input  [3:0] O1,
  input  [3:0] O2,
  input  [3:0] O3,
  input  [3:0] O4,
  input  [3:0] O5,
  input  [3:0] O6,
  input  [3:0] O7,
  output [3:0] O
);

  eightBitMux eightbitmux_1 (
    .S2(S2), .S1(S1), .S0(S0), .A0(O0[0]), .A1(O1[0]), .A2(O2[0]), .A3(O3[0]), .A4(O4[0]), .A5(O5[0]),
    .A6(O6[0]), .A7(O7[0]), .O(O[0]));
  eightBitMux eightbitmux_2 (
    .S2(S2), .S1(S1), .S0(S0), .A0(O0[1]), .A1(O1[1]), .A2(O2[1]), .A3(O3[1]), .A4(O4[1]), .A5(O5[1]),
    .A6(O6[1]), .A7(O7[1]), .O(O[1]));
  eightBitMux eightbitmux_3 (
    .S2(S2), .S1(S1), .S0(S0), .A0(O0[2]), .A1(O1[2]), .A2(O2[2]), .A3(O3[2]), .A4(O4[2]), .A5(O5[2]),
    .A6(O6[2]), .A7(O7[2]), .O(O[2]));
  eightBitMux eightbitmux_4 (
    .S2(S2), .S1(S1), .S0(S0), .A0(O0[3]), .A1(O1[3]), .A2(O2[3]), .A3(O3[3]), .A4(O4[3]), .A5(O5[3]),
    .A6(O6[3]), .A7(O7[3]), .O(O[3]));
endmodule

module RGST (
  input  [3:0] A,
  input  [3:0] B,
  input  MuxIn,
  input  CntrlBfr,
  output [3:0] O
);

  wire clock_1_out, controlled_buffer_1_out;
  wire [3:0] multiplexer_1_out;

  Clock clock_1 (.out(clock_1_out));
  Multiplexer #(.width(4)) multiplexer_1 (.in0(A), .in1(B), .out(multiplexer_1_out), .sel(MuxIn));
  assign controlled_buffer_1_out = CntrlBfr ? clock_1_out : 1'bz;  // Controlled_Buffer controlled_buffer_1
  D_Flip_Flop d_ff_1 (.D(multiplexer_1_out[0]), .clk(controlled_buffer_1_out), .Q(O[0]));  // open: Qn, preset, reset
  D_Flip_Flop d_ff_2 (.D(multiplexer_1_out[1]), .clk(controlled_buffer_1_out), .Q(O[1]));  // open: Qn, preset, reset
  D_Flip_Flop d_ff_3 (.D(multiplexer_1_out[2]), .clk(controlled_buffer_1_out), .Q(O[2]));  // open: Qn, preset, reset
  D_Flip_Flop d_ff_4 (.D(multiplexer_1_out[3]), .clk(controlled_buffer_1_out), .Q(O[3]));  // open: Qn, preset, reset
endmodule

module fourBitOR (
  input  [3:0] A,
  output AorB
);

  wire or_1_out, or_2_out;

  or or_1 (or_1_out, A[0], A[1]);
  or or_2 (or_2_out, A[2], A[3]);
  or or_3 (AorB, or_1_out, or_2_out);
endmodule

module eightBitOrSelf (
  input  [7:0] A,
  output AorB
);

  wire or_1_out, or_2_out, or_3_out, or_4_out, or_5_out, or_6_out;

  or or_1 (or_1_out, A[0], A[1]);
  or or_2 (or_2_out, A[2], A[3]);
  or or_3 (or_3_out, A[4], A[5]);
  or or_4 (or_4_out, A[6], A[7]);
  or or_5 (or_5_out, or_1_out, or_2_out);
  or or_6 (or_6_out, or_3_out, or_4_out);
  or or_7 (AorB, or_5_out, or_6_out);
endmodule

module fourBitAdd (
  input  Cin,
  input  [3:0] in_2,
  input  [3:0] in_3,
  output [3:0] out_4
);

  wire add_1_cout, add_2_cout, add_3_cout;

  Add add_1 (.A(in_2[0]), .B(in_3[0]), .Cin(Cin), .Sum(out_4[0]), .Cout(add_1_cout));
  Add add_2 (.A(in_2[1]), .B(in_3[1]), .Cin(add_1_cout), .Sum(out_4[1]), .Cout(add_2_cout));
  Add add_3 (.A(in_2[2]), .B(in_3[2]), .Cin(add_2_cout), .Sum(out_4[2]), .Cout(add_3_cout));
  Add add_4 (.A(in_2[3]), .B(in_3[3]), .Cin(add_3_cout), .Sum(out_4[3]));  // open: Cout
endmodule

module rgstNew (
  input  [3:0] Inp,
  input  Clk,
  input  RST,
  output [3:0] O
);

  D_Flip_Flop d_ff_1 (.D(Inp[0]), .clk(Clk), .Q(O[0]), .reset(RST));  // open: Qn, preset
  D_Flip_Flop d_ff_2 (.D(Inp[1]), .clk(Clk), .Q(O[1]), .reset(RST));  // open: Qn, preset
  D_Flip_Flop d_ff_3 (.D(Inp[2]), .clk(Clk), .Q(O[2]), .reset(RST));  // open: Qn, preset
  D_Flip_Flop d_ff_4 (.D(Inp[3]), .clk(Clk), .Q(O[3]), .reset(RST));  // open: Qn, preset
endmodule

module RgstOneBit (
  input  [3:0] Inp,
  input  CntrlBf,
  input  RST,
  output [3:0] O
);

  wire clock_1_out, controlled_buffer_1_out;

  Clock clock_1 (.out(clock_1_out));
  assign controlled_buffer_1_out = CntrlBf ? clock_1_out : 1'bz;  // Controlled_Buffer controlled_buffer_1
  D_Flip_Flop d_ff_1 (.D(Inp[0]), .clk(controlled_buffer_1_out), .Q(O[0]), .reset(RST));  // open: Qn, preset
  D_Flip_Flop d_ff_2 (.D(Inp[1]), .clk(controlled_buffer_1_out), .Q(O[1]), .reset(RST));  // open: Qn, preset
  D_Flip_Flop d_ff_3 (.D(Inp[2]), .clk(controlled_buffer_1_out), .Q(O[2]), .reset(RST));  // open: Qn, preset
  D_Flip_Flop d_ff_4 (.D(Inp[3]), .clk(controlled_buffer_1_out), .Q(O[3]), .reset(RST));  // open: Qn, preset
endmodule

module fourBitSubCons (
  input  [3:0] A,
  output [3:0] O,
  output Bout
);

  wire sub_1_bout, sub_2_bout, sub_3_bout;

  Sub sub_1 (.A(A[0]), .B(1'b1), .Bin(1'b0), .O(O[0]), .Bout(sub_1_bout));
  Sub sub_2 (.A(A[1]), .B(1'b0), .Bin(sub_1_bout), .O(O[1]), .Bout(sub_2_bout));
  Sub sub_3 (.A(A[2]), .B(1'b0), .Bin(sub_2_bout), .O(O[2]), .Bout(sub_3_bout));
  Sub sub_4 (.A(A[3]), .B(1'b0), .Bin(sub_3_bout), .O(O[3]), .Bout(Bout));
endmodule

module fourBitCounter (
  input  CLK,
  input  RST,
  output [3:0] A
);

  wire d_ff_1_qn, d_ff_2_qn, d_ff_3_qn, d_ff_4_qn;

  D_Flip_Flop d_ff_1 (.D(d_ff_1_qn), .clk(CLK), .Q(A[0]), .Qn(d_ff_1_qn), .reset(RST));  // open: preset
  D_Flip_Flop d_ff_2 (.D(d_ff_2_qn), .clk(d_ff_1_qn), .Q(A[1]), .Qn(d_ff_2_qn), .reset(RST));  // open: preset
  D_Flip_Flop d_ff_3 (.D(d_ff_3_qn), .clk(d_ff_2_qn), .Q(A[2]), .Qn(d_ff_3_qn), .reset(RST));  // open: preset
  D_Flip_Flop d_ff_4 (.D(d_ff_4_qn), .clk(d_ff_3_qn), .Q(A[3]), .Qn(d_ff_4_qn));  // open: preset, reset
endmodule

module threeBitHelper (
  input  [2:0] Inp,
  output I1,
  output I2,
  output I3,
  output I4,
  output I5,
  output I6,
  output I7,
  output I8
);

  ThreeBitEqual O1 (.A(Inp), .B(3'b000), .O(I1));
  ThreeBitEqual O2 (.A(Inp), .B(3'b001), .O(I2));
  ThreeBitEqual O3 (.A(Inp), .B(3'b010), .O(I3));
  ThreeBitEqual O4 (.A(Inp), .B(3'b011), .O(I4));
  ThreeBitEqual O5 (.A(Inp), .B(3'b100), .O(I5));
  ThreeBitEqual O6 (.A(Inp), .B(3'b101), .O(I6));
  ThreeBitEqual O7 (.A(Inp), .B(3'b110), .O(I7));
  ThreeBitEqual O8 (.A(Inp), .B(3'b111), .O(I8));
endmodule

module VendingMachine1 (
  input  S0,
  input  S1,
  input  S2,
  input  Item1,
  input  Item2,
  input  Item3,
  input  Item4,
  input  Item5,
  input  Item6,
  input  Item7,
  input  Item8,
  input  [2:0] B,
  output ItemAndMoney,
  output [2:0] A
);

  wire and_2_out, clock_1_out, eightbitmux_1_o, Money_out, not_1_out, not_2_out, sr_latch_1_q,
       threebitequal_1_o;

  Button Money (.out(Money_out));
  SR_latch sr_latch_1 (.R(threebitequal_1_o), .S(Money_out), .Q(sr_latch_1_q));
  not not_1 (not_1_out, sr_latch_1_q);
  LED NoMoney (.in(not_1_out));
  not not_2 (not_2_out, eightbitmux_1_o);
  LED NoItem (.in(not_2_out));
  eightBitMux eightbitmux_1 (
    .S2(S0), .S1(S1), .S0(S2), .A0(Item1), .A1(Item2), .A2(Item3), .A3(Item4), .A4(Item5), .A5(Item6),
    .A6(Item7), .A7(Item8), .O(eightbitmux_1_o));
  and and_1 (ItemAndMoney, eightbitmux_1_o, sr_latch_1_q);
  Clock clock_1 (.out(clock_1_out));
  and and_2 (and_2_out, ItemAndMoney, clock_1_out);
  ThreeBitEqual threebitequal_1 (.A(A), .B(B), .O(threebitequal_1_o));
  DFlipFlopWithComp dflipflopwithcomp_1 (.CLK(and_2_out), .RST(threebitequal_1_o), .A(A));
endmodule

module VendingMachine2 (
  input  in_1,
  input  [3:0] in_2,
  input  [3:0] in_3,
  input  [3:0] Qn,
  input  [3:0] Price,
  input  [2:0] in_6,
  input  in_7,
  input  in_8,
  output [3:0] out_9,
  output [2:0] out_10,
  output [3:0] out_11,
  output out_12,
  output [3:0] out_13,
  output [3:0] out_14
);

  wire and_1_out, button_1_out, clock_1_out, comparator_1_eq, comparator_1_gt, comparator_1_lt,
       fourbitor_1_aorb, fourbitor_2_aorb, fourbitor_3_aorb, not_1_out, not_2_out, not_3_out, not_4_out,
       threebitequal_1_o;
  wire [3:0] controlled_buffer_1_out, fourbitadd_1_out_4;

  Button button_1 (.out(button_1_out));
  assign controlled_buffer_1_out = button_1_out ? out_14 : 4'bz;  // Controlled_Buffer controlled_buffer_1
  fourBitAdd fourbitadd_1 (.Cin(in_1), .in_2(in_2), .in_3(in_3), .out_4(fourbitadd_1_out_4));
  SR_latch sr_latch_1 (.R(threebitequal_1_o), .S(controlled_buffer_1_out[0]), .Q(out_11[0]));
  SR_latch sr_latch_2 (.R(threebitequal_1_o), .S(controlled_buffer_1_out[1]), .Q(out_11[1]));
  SR_latch sr_latch_3 (.R(threebitequal_1_o), .S(controlled_buffer_1_out[2]), .Q(out_11[2]));
  SR_latch sr_latch_4 (.R(threebitequal_1_o), .S(controlled_buffer_1_out[3]), .Q(out_11[3]));
  LED led_1 (.in(not_1_out));
  not not_1 (not_1_out, fourbitor_1_aorb);
  fourBitOR fourbitor_1 (.A(out_11), .AorB(fourbitor_1_aorb));
  RGST rgst_1 (.A(out_13), .B(fourbitadd_1_out_4), .MuxIn(in_7), .CntrlBfr(in_8), .O(out_14));
  Comparator #(.mode("unsigned"), .width(4)) comparator_1 (
    .a(out_11), .b(Price), .gt(comparator_1_gt), .eq(comparator_1_eq), .lt(comparator_1_lt));
  or or_1 (out_12, comparator_1_gt, comparator_1_eq);
  not not_2 (not_2_out, out_12);
  fourBitOR fourbitor_2 (.A(Qn), .AorB(fourbitor_2_aorb));
  fourBitOR fourbitor_3 (.A(Price), .AorB(fourbitor_3_aorb));
  LED led_2 (.in(not_2_out));
  Clock clock_1 (.out(clock_1_out));
  fourBitSub fourbitsub_1 (.Bin(1'b0), .A(out_11), .B(Price), .O(out_13));  // open: Bout
  not not_3 (not_3_out, fourbitor_2_aorb);
  LED led_3 (.in(not_3_out));
  not not_4 (not_4_out, fourbitor_3_aorb);
  LED led_4 (.in(not_4_out));
  and and_1 (and_1_out, out_12, clock_1_out);
  DFlipFlopWithComp dflipflopwithcomp_1 (.CLK(and_1_out), .RST(threebitequal_1_o), .A(out_10));
  fourBitSubCons fourbitsubcons_1 (.A(Qn), .O(out_9));  // open: Bout
  ThreeBitEqual threebitequal_1 (.A(out_10), .B(in_6), .O(threebitequal_1_o));
endmodule

module VendingMachineMain (
  input  C2,
  input  C1,
  input  C0,
  input  [3:0] Qn0,
  input  [3:0] P0,
  input  [3:0] Qn1,
  input  [3:0] P1,
  input  [3:0] P2,
  input  [3:0] P3,
  input  [3:0] Qn2,
  input  [3:0] P4,
  input  [3:0] P5,
  input  [3:0] Qn3,
  input  [3:0] P6,
  input  [3:0] P7,
  input  [3:0] Qn4,
  input  [3:0] Qn5,
  input  [3:0] Qn6,
  input  [3:0] Qn7,
  input  in_20,
  input  [3:0] Comp,
  input  [3:0] Money,
  input  [3:0] MoneyToAdd,
  input  in_24,
  output [3:0] out_25,
  output [7:0] out_26,
  output [3:0] Qn,
  output [3:0] out_28,
  output out_29,
  output [3:0] out_30,
  output [3:0] out_31,
  output [3:0] out_32,
  output [3:0] out_33,
  output [3:0] out_34,
  output [3:0] out_35,
  output [3:0] out_36,
  output [3:0] Counter,
  output out_38,
  output [3:0] out_39
);

  wire and_1_out, button_1_out, button_2_out, clock_1_out, comparator_1_eq, comparator_1_gt,
       fourbitor_1_aorb, fourbitor_2_aorb, not_1_out, not_2_out, not_3_out, or_1_out;
  wire [3:0] controlled_buffer_1_out, controlled_buffer_2_out, controlled_buffer_3_out, fourbitadd_1_out_4,
       fourbitsub_1_o, multifourbitmux_1_o, multiplexer_1_out, rgstonebit_1_o, rgstonebit_2_o,
       rgstonebit_3_o, rgstonebit_4_o, rgstonebit_5_o, rgstonebit_6_o, rgstonebit_7_o, rgstonebit_8_o;

  Button button_1 (.out(button_1_out));
  Multiplexer #(.width(4)) multiplexer_1 (.in0(Money), .in1(fourbitsub_1_o), .out(multiplexer_1_out), .sel(in_24));
  fourBitAdd fourbitadd_1 (.Cin(1'b0), .in_2(multiplexer_1_out), .in_3(MoneyToAdd), .out_4(fourbitadd_1_out_4));
  RgstOneBit rgstonebit_1 (.Inp(Qn0), .CntrlBf(button_1_out), .RST(in_20), .O(rgstonebit_1_o));
  RgstOneBit rgstonebit_2 (.Inp(Qn1), .CntrlBf(button_1_out), .RST(in_20), .O(rgstonebit_2_o));
  RgstOneBit rgstonebit_3 (.Inp(Qn2), .CntrlBf(button_1_out), .RST(in_20), .O(rgstonebit_3_o));
  RgstOneBit rgstonebit_4 (.Inp(Qn3), .CntrlBf(button_1_out), .RST(in_20), .O(rgstonebit_4_o));
  RgstOneBit rgstonebit_5 (.Inp(Qn4), .CntrlBf(button_1_out), .RST(in_20), .O(rgstonebit_5_o));
  RgstOneBit rgstonebit_6 (.Inp(Qn5), .CntrlBf(button_1_out), .RST(in_20), .O(rgstonebit_6_o));
  RgstOneBit rgstonebit_7 (.Inp(Qn6), .CntrlBf(button_1_out), .RST(in_20), .O(rgstonebit_7_o));
  RgstOneBit rgstonebit_8 (.Inp(Qn7), .CntrlBf(button_1_out), .RST(in_20), .O(rgstonebit_8_o));
  Button button_2 (.out(button_2_out));
  Comparator #(.mode("unsigned"), .width(4)) comparator_1 (
    .a(out_39), .b(out_25), .gt(comparator_1_gt), .eq(comparator_1_eq));  // open: lt
  assign controlled_buffer_1_out = or_1_out ? multifourbitmux_1_o : 4'bz;  // Controlled_Buffer controlled_buffer_1
  assign controlled_buffer_2_out = or_1_out ? out_39 : 4'bz;  // Controlled_Buffer controlled_buffer_2
  or or_1 (or_1_out, comparator_1_gt, comparator_1_eq);
  RgstOneBit rgstonebit_9 (.Inp(fourbitadd_1_out_4), .CntrlBf(button_2_out), .RST(out_38), .O(out_39));
  MultiFourBitMux multifourbitmux_1 (
    .S2(C2), .S1(C1), .S0(C0), .O0(rgstonebit_1_o), .O1(rgstonebit_2_o), .O2(rgstonebit_3_o),
    .O3(rgstonebit_4_o), .O4(rgstonebit_5_o), .O5(rgstonebit_6_o), .O6(rgstonebit_7_o), .O7(rgstonebit_8_o),
    .O(multifourbitmux_1_o));
  assign controlled_buffer_3_out = or_1_out ? multifourbitmux_1_o : 4'bz;  // Controlled_Buffer controlled_buffer_3
  Clock #(.highDuration(200), .lowDuration(200)) clock_1 (.out(clock_1_out));
  and and_1 (and_1_out, or_1_out, fourbitor_2_aorb, fourbitor_1_aorb, clock_1_out);
  fourBitSub fourbitsub_1 (
    .Bin(1'b0), .A(controlled_buffer_2_out), .B(controlled_buffer_1_out), .O(fourbitsub_1_o), .Bout(out_29));
  fourBitOR fourbitor_1 (.A(controlled_buffer_2_out), .AorB(fourbitor_1_aorb));
  fourBitOR fourbitor_2 (.A(controlled_buffer_1_out), .AorB(fourbitor_2_aorb));
  not not_1 (not_1_out, or_1_out);
  not not_2 (not_2_out, fourbitor_1_aorb);
  not not_3 (not_3_out, fourbitor_2_aorb);
  LED NoMoney (.in(not_2_out));
  LED NoQuantity (.in(not_3_out));
  fourBitSubCons fourbitsubcons_1 (.A(controlled_buffer_3_out), .O(Qn));  // open: Bout
  LED MoneyLessThanPrice (.in(not_1_out));
  Comparator #(.mode("unsigned"), .width(4)) comparator_2 (.a(Counter), .b(Comp), .eq(out_38));  // open: gt, lt
  fourBitCounter fourbitcounter_1 (.CLK(and_1_out), .RST(out_38), .A(Counter));
  MultiFourBitMux multifourbitmux_2 (
    .S2(C2), .S1(C1), .S0(C0), .O0(P0), .O1(P1), .O2(P2), .O3(P3), .O4(P4), .O5(P5), .O6(P6), .O7(P7),
    .O(out_25));
  Demultiplexer #(.select(3), .width(4)) demultiplexer_1 (
    .out0(out_28), .out1(out_30), .out2(out_31), .out3(out_32), .out4(out_33), .out5(out_34), .out6(out_35),
    .out7(out_36), .in(Qn), .sel({C2, C1, C0}));
  threeBitHelper threebithelper_1 (
    .Inp({C2, C1, C0}), .I1(out_26[0]), .I2(out_26[1]), .I3(out_26[2]), .I4(out_26[3]), .I5(out_26[4]),
    .I6(out_26[5]), .I7(out_26[6]), .I8(out_26[7]));
endmodule

module VendingMachinePRJ (
  input  S2,
  input  S1,
  input  S0,
  input  [3:0] Qn0,
  input  [3:0] Qn1,
  input  [3:0] Qn2,
  input  [3:0] Qn3,
  input  [3:0] Qn4,
  input  [3:0] Qn5,
  input  [3:0] P0,
  input  [3:0] Qn6,
  input  [3:0] P1,
  input  [3:0] P2,
  input  [3:0] P3,
  input  [3:0] P4,
  input  [3:0] P5,
  input  [3:0] P6,
  input  [3:0] Qn7,
  input  [3:0] P7,
  input  RST,
  input  [3:0] DMoney,
  input  [3:0] Comp,
  input  [3:0] MoneyToAdd,
  output [3:0] out_24,
  output [2:0] out_25,
  output [7:0] out_26,
  output [3:0] out_27,
  output [3:0] out_28,
  output [3:0] out_29,
  output [3:0] out_30,
  output [3:0] out_31,
  output [3:0] out_32,
  output [3:0] out_33,
  output [3:0] Counter,
  output out_35,
  output ImpossibleCarry
);

  wire and_1_out, and_2_out, and_3_out, clock_1_out, clock_2_out, clock_3_out, clock_4_out, comparator_1_eq,
       comparator_1_gt, comparator_1_lt, controlled_buffer_1_out, fourbitor_1_aorb, fourbitor_2_aorb,
       fourbitor_3_aorb, MoneyRead_out, not_1_out, not_2_out, not_3_out, or_1_out, or_2_out, Read_out,
       ResetMoney_out, UseRmngMoney_out, Write_out;
  wire [3:0] controlled_buffer_3_out, controlled_buffer_5_out, controlled_buffer_6_out,
       controlled_buffer_7_out, controlled_buffer_8_out, controlled_buffer_9_out, controlled_buffer_10_out,
       controlled_buffer_21_out, controlled_buffer_22_out, fourbitadd_1_out_4, rgstnew_2_o, rgstnew_3_o,
       rgstnew_4_o, rgstnew_5_o, rgstnew_6_o, rgstnew_7_o, rgstnew_8_o, rgstnew_9_o;

  assign controlled_buffer_1_out = Read_out ? clock_1_out : 1'bz;  // Controlled_Buffer controlled_buffer_1
  Clock clock_1 (.out(clock_1_out));
  Button ResetMoney (.out(ResetMoney_out));
  Button Read (.out(Read_out));
  Button MoneyRead (.out(MoneyRead_out));
  or or_1 (or_1_out, MoneyRead_out, UseRmngMoney_out);
  assign out_31 = MoneyRead_out ? DMoney : 4'bz;  // Controlled_Buffer controlled_buffer_2
  Clock clock_2 (.out(clock_2_out));
  assign controlled_buffer_3_out = Read_out ? Qn0 : 4'bz;  // Controlled_Buffer controlled_buffer_3
  assign out_24 = Read_out ? Qn1 : 4'bz;  // Controlled_Buffer controlled_buffer_4
  assign controlled_buffer_5_out = Read_out ? Qn2 : 4'bz;  // Controlled_Buffer controlled_buffer_5
  assign controlled_buffer_6_out = Read_out ? Qn3 : 4'bz;  // Controlled_Buffer controlled_buffer_6
  assign controlled_buffer_7_out = Read_out ? Qn4 : 4'bz;  // Controlled_Buffer controlled_buffer_7
  assign controlled_buffer_8_out = Read_out ? Qn5 : 4'bz;  // Controlled_Buffer controlled_buffer_8
  assign controlled_buffer_9_out = Read_out ? Qn6 : 4'bz;  // Controlled_Buffer controlled_buffer_9
  assign controlled_buffer_10_out = Read_out ? Qn7 : 4'bz;  // Controlled_Buffer controlled_buffer_10
  Button Write (.out(Write_out));
  Button UseRmngMoney (.out(UseRmngMoney_out));
  and and_1 (and_1_out, or_1_out, clock_2_out);
  and and_2 (and_2_out, ResetMoney_out, out_35);
  assign controlled_buffer_1_out = Write_out ? clock_3_out : 1'bz;  // Controlled_Buffer controlled_buffer_11
  Clock clock_3 (.out(clock_3_out));
  assign out_31 = UseRmngMoney_out ? out_32 : 4'bz;  // Controlled_Buffer controlled_buffer_12
  assign controlled_buffer_3_out = out_26[0] ? out_28 : 4'bz;  // Controlled_Buffer controlled_buffer_13
  assign out_24 = out_26[1] ? out_28 : 4'bz;  // Controlled_Buffer controlled_buffer_14
  assign controlled_buffer_5_out = out_26[2] ? out_28 : 4'bz;  // Controlled_Buffer controlled_buffer_15
  assign controlled_buffer_6_out = out_26[3] ? out_28 : 4'bz;  // Controlled_Buffer controlled_buffer_16
  assign controlled_buffer_7_out = out_26[4] ? out_28 : 4'bz;  // Controlled_Buffer controlled_buffer_17
  assign controlled_buffer_8_out = out_26[5] ? out_28 : 4'bz;  // Controlled_Buffer controlled_buffer_18
  assign controlled_buffer_9_out = out_26[6] ? out_28 : 4'bz;  // Controlled_Buffer controlled_buffer_19
  assign controlled_buffer_10_out = out_26[7] ? out_28 : 4'bz;  // Controlled_Buffer controlled_buffer_20
  rgstNew rgstnew_1 (.Inp(out_31), .Clk(and_1_out), .RST(and_2_out), .O(out_30));
  Clock clock_4 (.out(clock_4_out));
  fourBitAdd fourbitadd_1 (.Cin(1'b0), .in_2(out_30), .in_3(MoneyToAdd), .out_4(fourbitadd_1_out_4));
  assign controlled_buffer_21_out = or_2_out ? fourbitadd_1_out_4 : 4'bz;  // Controlled_Buffer controlled_buffer_21
  assign controlled_buffer_22_out = or_2_out ? out_29 : 4'bz;  // Controlled_Buffer controlled_buffer_22
  rgstNew rgstnew_2 (.Inp(controlled_buffer_3_out), .Clk(controlled_buffer_1_out), .RST(RST), .O(rgstnew_2_o));
  rgstNew rgstnew_3 (.Inp(out_24), .Clk(controlled_buffer_1_out), .RST(RST), .O(rgstnew_3_o));
  rgstNew rgstnew_4 (.Inp(controlled_buffer_5_out), .Clk(controlled_buffer_1_out), .RST(RST), .O(rgstnew_4_o));
  rgstNew rgstnew_5 (.Inp(controlled_buffer_6_out), .Clk(controlled_buffer_1_out), .RST(RST), .O(rgstnew_5_o));
  rgstNew rgstnew_6 (.Inp(controlled_buffer_7_out), .Clk(controlled_buffer_1_out), .RST(RST), .O(rgstnew_6_o));
  rgstNew rgstnew_7 (.Inp(controlled_buffer_8_out), .Clk(controlled_buffer_1_out), .RST(RST), .O(rgstnew_7_o));
  rgstNew rgstnew_8 (.Inp(controlled_buffer_9_out), .Clk(controlled_buffer_1_out), .RST(RST), .O(rgstnew_8_o));
  rgstNew rgstnew_9 (.Inp(controlled_buffer_10_out), .Clk(controlled_buffer_1_out), .RST(RST), .O(rgstnew_9_o));
  Comparator #(.mode("unsigned"), .width(4)) comparator_1 (
    .a(fourbitadd_1_out_4), .b(out_29), .gt(comparator_1_gt), .eq(comparator_1_eq), .lt(comparator_1_lt));
  or or_2 (or_2_out, comparator_1_gt, comparator_1_eq);
  Subtractor #(.width(4)) subtractor_1 (
    .a(controlled_buffer_21_out), .b(controlled_buffer_22_out), .out(out_32), .bout(ImpossibleCarry));  // open: bin
  and and_3 (and_3_out, or_2_out, fourbitor_1_aorb, fourbitor_2_aorb, clock_4_out);
  fourBitCounter fourbitcounter_1 (.CLK(and_3_out), .RST(out_35), .A(Counter));
  Subtractor #(.width(4)) subtractor_2 (.a(out_27), .b(4'b0001), .out(out_28));  // open: bin, bout
  threeBitHelper threebithelper_1 (
    .Inp({S2, S1, S0}), .I1(out_26[0]), .I2(out_26[1]), .I3(out_26[2]), .I4(out_26[3]), .I5(out_26[4]),
    .I6(out_26[5]), .I7(out_26[6]), .I8(out_26[7]));
  MultiFourBitMux multifourbitmux_1 (
    .S2(S2), .S1(S1), .S0(S0), .O0(rgstnew_2_o), .O1(rgstnew_3_o), .O2(rgstnew_4_o), .O3(rgstnew_5_o),
    .O4(rgstnew_6_o), .O5(rgstnew_7_o), .O6(rgstnew_8_o), .O7(rgstnew_9_o), .O(out_27));
  MultiFourBitMux multifourbitmux_2 (
    .S2(S2), .S1(S1), .S0(S0), .O0(P0), .O1(P1), .O2(P2), .O3(P3), .O4(P4), .O5(P5), .O6(P6), .O7(P7),
    .O(out_29));
  Comparator #(.mode("unsigned"), .width(4)) comparator_2 (.a(Counter), .b(Comp), .eq(out_35));  // open: gt, lt
  LED NoQn (.in(not_1_out));
  not not_1 (not_1_out, fourbitor_1_aorb);
  fourBitOR fourbitor_1 (.A(out_27), .AorB(fourbitor_1_aorb));
  LED NoPrice (.in(not_2_out));
  not not_2 (not_2_out, fourbitor_2_aorb);
  fourBitOR fourbitor_2 (.A(out_29), .AorB(fourbitor_2_aorb));
  LED NoMoney (.in(not_3_out));
  not not_3 (not_3_out, fourbitor_3_aorb);
  fourBitOR fourbitor_3 (.A(fourbitadd_1_out_4), .AorB(fourbitor_3_aorb));
  LED MoneyLessThanPrice (.in(comparator_1_lt));

  assign out_25 = {S2, S1, S0};
  assign out_33 = out_32;
endmodule
